# Fritzing sketch Electronic Wiring Diagram (saved by Fritzing 0.9.3b)
breadboards: 2

parts:
  Part1 = Adafruit Feather nRF52 [part_number="Adafruit #3406"]
  DS1 = DS18B20 1-Wire Temperature Sensor [part_number=DS18B20]
  R1 = Resistor [tolerance=±5% resistance=4.7k package=THT]
  Part2 = Adafruit Feather nRF52 [part_number="Adafruit #3406"]
  U1 = NodeMCU V1.0

nets:
  3.3V: Part1.3.3V, DS1.VDD, R1.Pin_1
  GND: Part1.GND, DS1.GND
  N1: Part1.P0.07, DS1.DQ, R1.Pin_0
  N2: Part2.TXD, U1.RX
  N3: Part2.RXD, U1.TX

notes:
  Black wire = GND
  Red wire = 3v
  Green wire = pin 7
  Resistor = 4.7k Ohms
  Sensor = DS18B20
  Feather to NodeMCU
  Yellow wire = Tx to RX
  Orange wire = Rx to Tx

custom parts:
  NodeMCU V1.0: ESP8266 based NodeMCU
